// Logisim project control-logic.circ as structural Verilog: 1 circuit, main circuit control_logic
module control_logic (
  input  [31:0] Instruction,
  input  BrEq,
  input  BrLt,
  output PCSel,
  output RegWEn,
  output [2:0] ImmSel,
  output BrUn,
  output ASel,
  output BSel,
  output [3:0] ALUSel,
  output MemWEn,
  output [1:0] WBSel
);

  wire and_2_out, and_3_out, and_4_out, and_5_out, and_6_out, and_7_out, comparator_1_eq, comparator_2_eq,
       comparator_3_eq, comparator_4_eq, comparator_5_eq, comparator_6_eq, comparator_7_eq, comparator_8_eq,
       comparator_9_eq, comparator_10_eq, comparator_11_eq, comparator_12_eq, comparator_13_eq,
       comparator_14_eq, comparator_15_eq, comparator_16_eq, comparator_17_eq, comparator_18_eq,
       comparator_19_eq, isSrai, Itype, or_4_out, or_5_out, Rtype, WBSelALUout;
  wire [1:0] multiplexer_1_out;
  wire [3:0] bit_extender_1_out, multiplexer_3_out;

  Comparator #(.width(7)) comparator_1 (.a(Instruction[6:0]), .b(7'b0010011), .eq(comparator_1_eq));  // open: gt, lt
  Comparator #(.width(7)) comparator_2 (.a(Instruction[6:0]), .b(7'b0000011), .eq(comparator_2_eq));  // open: gt, lt
  Comparator #(.width(7)) comparator_3 (.a(Instruction[6:0]), .b(7'b1100111), .eq(comparator_3_eq));  // open: gt, lt
  Comparator #(.width(7)) comparator_4 (.a(Instruction[6:0]), .b(7'b0110011), .eq(comparator_4_eq));  // open: gt, lt
  Comparator #(.width(7)) comparator_5 (.a(Instruction[6:0]), .b(7'b0010011), .eq(comparator_5_eq));  // open: gt, lt
  buf or_1 (WBSelALUout, comparator_5_eq);  // OR_Gate
  or or_2 (Itype, comparator_1_eq, comparator_2_eq, comparator_3_eq);
  and and_1 (Rtype, comparator_4_eq, 1'b1);
  or or_3 (RegWEn, comparator_1_eq, comparator_2_eq);
  Comparator #(.width(3)) comparator_6 (.a(Instruction[14:12]), .b(3'b000), .eq(comparator_6_eq));  // open: gt, lt
  Comparator #(.width(3)) comparator_7 (.a(Instruction[14:12]), .b(3'b001), .eq(comparator_7_eq));  // open: gt, lt
  Multiplexer #(.width(2)) multiplexer_1 (.in0(2'b00), .in1(2'b01), .out(multiplexer_1_out), .sel(WBSelALUout));
  Comparator #(.width(3)) comparator_8 (.a(Instruction[14:12]), .b(3'b010), .eq(comparator_8_eq));  // open: gt, lt
  Comparator #(.width(3)) comparator_9 (.a(Instruction[14:12]), .b(3'b100), .eq(comparator_9_eq));  // open: gt, lt
  Comparator #(.width(3)) comparator_10 (.a(Instruction[14:12]), .b(3'b101), .eq(comparator_10_eq));  // open: gt, lt
  and and_2 (and_2_out, comparator_2_eq, comparator_6_eq);
  and and_3 (and_3_out, comparator_2_eq, comparator_7_eq);
  and and_4 (and_4_out, comparator_2_eq, comparator_8_eq);
  and and_5 (and_5_out, comparator_2_eq, comparator_9_eq);
  and and_6 (and_6_out, comparator_2_eq, comparator_10_eq);
  Multiplexer #(.width(2)) multiplexer_2 (.in0(2'b01), .in1(multiplexer_1_out), .out(WBSel), .sel(MemWEn));
  or or_4 (or_4_out, and_2_out, and_3_out, and_4_out, and_5_out, and_6_out);
  not not_1 (MemWEn, or_4_out);
  Comparator #(.width(7)) comparator_11 (.a(Instruction[6:0]), .b(7'b1100011), .eq(comparator_11_eq));  // open: gt, lt
  assign bit_extender_1_out = {{1{1'b0}}, Instruction[14:12]};  // Bit_Extender bit_extender_1
  Comparator #(.width(3)) comparator_12 (.a(Instruction[14:12]), .b(3'b101), .eq(comparator_12_eq));  // open: gt, lt
  Comparator #(.width(7)) comparator_13 (
    .a(Instruction[31:25]), .b(7'b0100000), .eq(comparator_13_eq));  // open: gt, lt
  and and_7 (and_7_out, Itype, 1'b1);
  Comparator #(.width(7)) comparator_14 (.a(Instruction[6:0]), .b(7'b1100011), .eq(comparator_14_eq));  // open: gt, lt
  Comparator #(.width(7)) comparator_15 (.a(Instruction[6:0]), .b(7'b0010111), .eq(comparator_15_eq));  // open: gt, lt
  Comparator #(.width(7)) comparator_16 (.a(Instruction[6:0]), .b(7'b0110111), .eq(comparator_16_eq));  // open: gt, lt
  Comparator #(.width(7)) comparator_17 (.a(Instruction[6:0]), .b(7'b1101111), .eq(comparator_17_eq));  // open: gt, lt
  Multiplexer #(.width(4)) multiplexer_3 (
    .in0(4'b0000), .in1(bit_extender_1_out), .out(multiplexer_3_out), .sel(or_5_out));
  or or_5 (or_5_out, 1'b0, Itype);
  and and_8 (isSrai, Itype, comparator_12_eq, comparator_13_eq);
  Comparator #(.width(7)) comparator_18 (.a(Instruction[6:0]), .b(7'b0010111), .eq(comparator_18_eq));  // open: gt, lt
  Comparator #(.width(7)) comparator_19 (.a(Instruction[6:0]), .b(7'b1101111), .eq(comparator_19_eq));  // open: gt, lt
  or or_6 (BSel, and_7_out, comparator_14_eq, comparator_15_eq, comparator_16_eq, comparator_17_eq);
  Multiplexer #(.width(4)) multiplexer_4 (.in0(multiplexer_3_out), .in1(4'b1101), .out(ALUSel), .sel(isSrai));
  or or_7 (ASel, comparator_11_eq, comparator_18_eq, comparator_19_eq);

  assign ImmSel = 3'b000;

  // Other names for the same wires on the sheet: opcode[6:0] = Instruction[6:0]; rd[4:0] = Instruction[11:7];
  //   func3[2:0] = Instruction[14:12]; rs1[4:0] = Instruction[19:15]; rs2[4:0] = Instruction[24:20];
  //   func7[6:0] = Instruction[31:25]

  // Notes on the sheet:
  //   INPUTS to your circuit
  //   DON'T CHANGE THE LOCATIONS OF THE INPUTS AND OUTPUTS!
  //   lw
  //   lbu
  //   OUTPUT from your circuit
  //   | 0b0000011 | lb, lh, lw, ld, lbu, lhu, lwu 
  //   lb
  //   lh
  //   lhu
  //   Instruction Decode
  //   BSel is 1 for any of the following opcodes
  //   | 0b1100111 | jalr 
  //   | 0b0010111 | auipc 
  //   | 0b0110111 | lui
  //   | 0b1101111 | jal
  //   Sign extend if true (srai)
  //   B operand is immediate
  //   | 0b0010011 | addi, slli, xori, srli, srai, ori, andi
  //   | 0b0000011 | lb, lh, lw, ld, lbu, lhu, lwu
  //   | 0b1100011 | beq, bne, blt, bge, bltu, bgeu
  //   Select a program counter reference to use for the A Operand
  //   This should pass the value 13 to the alu if we're dealing with srai
endmodule
